// Logisim project hw_vga_sim.circ as structural Verilog: 8 circuits, main circuit main
module main (
  input  nRST
);

  wire CLK, HBeginActive, HBeginPulse, HCOUNT_END, HEndActive, HEndPulse, HVisEnd, readout_1_active,
       readout_1_count0, readout_1_count1, readout_1_phase, readout_1_updaterowbegincp, sync_1_hsync_out,
       sync_1_hvis, sync_1_vis, sync_1_vvis, VActive, VBeginPulse, VCOUNT_END, VCOUNT_ZERO, VEndActive,
       VEndPulse, VSync, VVisEnd;
  wire [11:0] HCOUNT_OUT, VCOUNT_OUT;
  wire [12:0] readout_1_readoutaddr, readout_1_rowbeginaddr;
  wire [15:0] bit_extender_1_out, bit_extender_2_out;

  Clock u_CLK (.out(CLK));
  LED led_1 (.in(sync_1_hsync_out));
  Sync sync_1 (
    .CLK(CLK), .nRST(nRST), .HBeginPulse(HBeginPulse), .HEndPulse(HEndPulse), .VBeginPulse(VBeginPulse),
    .VEndPulse(VEndPulse), .HCOUNT_END(HCOUNT_END), .VCOUNT_ZERO(VCOUNT_ZERO), .HVisEnd(HVisEnd),
    .VVisEnd(VVisEnd), .VCOUNT_END(VCOUNT_END), .VEndActive(VEndActive), .HSYNC_OUT(sync_1_hsync_out),
    .VSYNC_OUT(VSync), .HVis(sync_1_hvis), .VVis(sync_1_vvis), .Vis(sync_1_vis), .VActive(VActive));
  LED led_2 (.in(VSync));
  LED led_3 (.in(sync_1_hvis));
  LED led_4 (.in(sync_1_vvis));
  LED led_5 (.in(sync_1_vis));
  HCount hcount_1 (
    .CLK(CLK), .nRST(nRST), .HCOUNT_OUT(HCOUNT_OUT), .HCOUNT_END(HCOUNT_END), .BeginPulse(HBeginPulse),
    .EndPulse(HEndPulse), .HVisEnd(HVisEnd), .BeginActive(HBeginActive), .EndActive(HEndActive));
  VCount vcount_1 (
    .CLK(CLK), .nRST(nRST), .HCOUNT_END(HCOUNT_END), .VCOUNT_INCR(HEndPulse), .VCOUNT_OUT(VCOUNT_OUT),
    .VCOUNT_END(VCOUNT_END), .BeginPulse(VBeginPulse), .EndPulse(VEndPulse), .VVisEnd(VVisEnd),
    .VCOUNT_ZERO(VCOUNT_ZERO), .VEndActive(VEndActive));
  ROM #(.addrWidth(13)) VRAM (.addr(readout_1_readoutaddr));  // open: data
  assign bit_extender_1_out = {{3{1'b0}}, readout_1_rowbeginaddr};  // Bit_Extender bit_extender_1
  Hex_Digit_Display hex_digit_display_1 (.value(bit_extender_1_out[15:12]));  // open: dp
  Hex_Digit_Display hex_digit_display_2 (.value(HCOUNT_OUT[11:8]));  // open: dp
  Hex_Digit_Display hex_digit_display_3 (.value(VCOUNT_OUT[11:8]));  // open: dp
  Hex_Digit_Display hex_digit_display_4 (.value(bit_extender_1_out[7:4]));  // open: dp
  Hex_Digit_Display hex_digit_display_5 (.value(bit_extender_1_out[11:8]));  // open: dp
  ROM #(.addrWidth(12)) Font ();  // open: addr, data
  Hex_Digit_Display hex_digit_display_6 (.value(HCOUNT_OUT[7:4]));  // open: dp
  Hex_Digit_Display hex_digit_display_7 (.value(HCOUNT_OUT[3:0]));  // open: dp
  Hex_Digit_Display hex_digit_display_8 (.value(VCOUNT_OUT[7:4]));  // open: dp
  Hex_Digit_Display hex_digit_display_9 (.value(VCOUNT_OUT[3:0]));  // open: dp
  Hex_Digit_Display hex_digit_display_10 (.value(bit_extender_1_out[3:0]));  // open: dp
  Hex_Digit_Display hex_digit_display_11 (.value(bit_extender_2_out[15:12]));  // open: dp
  Readout readout_1 (
    .VSync(VSync), .CLK(CLK), .nRST(nRST), .VActive(VActive), .HBeginActive(HBeginActive),
    .HEndActive(HEndActive), .VCOUNT(VCOUNT_OUT[3:0]), .HBeginPulse(HBeginPulse), .Active(readout_1_active),
    .Count0(readout_1_count0), .Count1(readout_1_count1), .Phase(readout_1_phase),
    .ReadoutAddr(readout_1_readoutaddr), .RowBeginAddr(readout_1_rowbeginaddr),
    .UpdateRowBeginCP(readout_1_updaterowbegincp));
  Hex_Digit_Display hex_digit_display_12 (.value(bit_extender_2_out[11:8]));  // open: dp
  Hex_Digit_Display hex_digit_display_13 (.value(bit_extender_2_out[7:4]));  // open: dp
  LED led_6 (.in(readout_1_active));
  LED led_7 (.in(readout_1_count0));
  LED led_8 (.in(readout_1_count1));
  LED led_9 (.in(readout_1_phase));
  LED led_10 (.in(readout_1_updaterowbegincp));
  Hex_Digit_Display hex_digit_display_14 (.value(bit_extender_2_out[3:0]));  // open: dp
  assign bit_extender_2_out = {{3{1'b0}}, readout_1_readoutaddr};  // Bit_Extender bit_extender_2

  // Notes on the sheet:
  //   Row begin address
  //   contents of Font (hex, n*v repeats v):
  //   18*0 7c 82 82 aa 82 82 ba 92 82 7c 6*0 7c fe fe d6 fe fe c6 ee fe 7c 9*0 6c fe fe 7c 38 10 9*0 10 38
  //   7c fe 7c 38 10 9*0 38 38 38 ee ee ee 10 38 8*0 10 38 7c fe fe 54 10 38 10*0 18 3c 3c 18 6*0 6*ff e7
  //   c3 c3 e7 6*ff 5*0 3c 66 42 42 66 3c 5*0 5*ff c3 99 bd bd 99 c3 5*ff 0 0 1e 6 a 10 10 7c 82 82 82 7c
  //   6*0 7c 82 82 82 7c 10 10 7c 10 10 6*0 1e 12 1e 4*10 f0 f0 e0 6*0 3e 22 3e 22 22 22 2e ee ec c0 6*0
  //   10 92 7c 44 82 82 82 44 7c 92 10 8*0 c0 e0 f0 f8 f0 e0 c0 9*0 18 38 78 f8 78 38 18 6*0 10 38 54 92
  //   10 10 92 54 38 10 6*0 7*44 0 44 44 6*0 7e f2 f2 f2 72 5*12 5*0 78 84 40 30 48 84 84 48 30 8 84 78
  //   11*0 4*fe 6*0 10 38 54 92 10 10 92 54 38 fe 6*0 10 38 54 92 6*10 6*0 6*10 92 54 38 10 8*0 10 8 4 fe
  //   4 8 10 9*0 10 20 40 fe 40 20 10 11*0 80 80 80 fe 11*0 24 42 ff 42 24 11*0 10 38 7c fe fe 11*0 fe fe
  //   7c 38 10 24*0 7*10 0 10 10 5*0 4*48 14*0 44 44 fe 44 44 44 fe 44 44 5*0 10 10 7c 92 90 80 7c 2 12 92
  //   7c 10 10 5*0 60 f2 64 8 10 20 4c 9e c 6*0 30 48 48 48 32 4a 84 84 84 7a 5*0 10 10 10 20 13*0 8 10
  //   6*20 10 8 6*0 20 10 6*8 10 20 8*0 10 54 38 fe 38 54 10 9*0 10 10 10 fe 10 10 10 15*0 10 10 10 20 9*0
  //   fe 18*0 30 30 9*0 2 4 8 10 20 40 80 6*0 38 44 82 82 92 92 82 82 44 38 6*0 10 30 50 6*10 7c 6*0 7c 82
  //   2 2 4 8 10 20 40 fe 6*0 7c 82 2 2 3c 2 2 2 82 7c 6*0 4 c 14 24 44 84 fe 4 4 4 6*0 fe 80 80 80 fc 82
  //   2 2 82 7c 6*0 7c 80 80 80 fc 4*82 7c 6*0 fe 2 2 4 8 5*10 6*0 7c 82 82 44 7c 4*82 7c 6*0 7c 4*82 7e 2
  //   2 2 7c 9*0 10 10 0 0 0 10 10 9*0 10 10 0 0 0 10 10 10 20 5*0 4 8 10 20 40 20 10 8 4 9*0 fe 0 0 fe
  //   10*0 40 20 10 8 4 8 10 20 40 6*0 7c 82 82 2 c 10 10 0 10 10 6*0 7c 82 82 ba aa aa 9c 80 80 7c 6*0 38
  //   44 82 82 82 fe 4*82 6*0 fc 82 82 82 fc 4*82 fc 6*0 7c 82 5*80 82 82 7c 6*0 f8 84 6*82 84 f8 6*0 fe
  //   80 80 80 fc 4*80 fe 6*0 fe 80 80 80 fc 5*80 6*0 7c 82 80 80 9e 4*82 7e 6*0 4*82 fe 5*82 6*0 7c 8*10
  //   7c 6*0 3e 7*4 84 78 6*0 84 88 90 a0 c0 a0 90 88 84 82 6*0 9*80 fe 6*0 82 c6 aa 92 92 5*82 6*0 82 c2
  //   a2 92 8a 86 4*82 6*0 7c 8*82 7c 6*0 fc 82 82 82 fc 5*80 6*0 7c 5*82 92 92 92 7c 8 4 4*0 fc 82 82 82
  //   fc 84 4*82 6*0 7c 82 80 60 30 c 2 82 82 7c 6*0 fe 9*10 6*0 9*82 7c 6*0 7*82 44 28 10 6*0 5*82 92 92
  //   92 aa 44 6*0 82 82 44 28 10 28 44 82 82 82 6*0 82 82 82 44 28 5*10 6*0 fe 2 4 8 10 20 40 80 80 fe
  //   6*0 38 8*20 38 9*0 80 40 20 10 8 4 2 6*0 38 8*8 38 4*0 10 28 44 82 25*0 fe 0 0 0 20 20 20 10 16*0 78
  //   4 4 7c 84 84 7e 6*0 80 80 80 bc c2 4*82 fc 9*0 7c 82 80 80 80 82 7c 6*0 2 2 2 7a 86 4*82 7e 9*0 7c
  //   82 82 fe 80 80 7c 6*0 1c 20 20 f8 6*20 9*0 7e 4*82 86 7a 2 2 7c 0 0 0 80 80 80 bc c2 5*82 6*0 10 10
  //   0 70 5*10 7c 6*0 8 8 0 38 8*8 70 0 0 0 80 80 80 86 98 e0 90 88 84 82 6*0 60 8*20 1c 9*0 ec 6*92 9*0
  //   bc c2 5*82 9*0 7c 5*82 7c 9*0 bc c2 82 82 82 c2 bc 80 80 80 6*0 7e 4*82 86 7a 2 2 2 6*0 bc c2 5*80
  //   9*0 7e 80 80 7c 2 2 fc 7*0 20 20 fc 5*20 1c 9*0 5*82 86 7a 9*0 4*82 44 28 10 9*0 82 82 82 92 92 92
  //   6c 9*0 82 44 28 10 28 44 82 9*0 5*82 86 7a 2 2 7c 6*0 fe 4 8 10 20 40 fe 6*0 c 10 10 10 60 4*10 c
  //   5*0 14*10 0 0 0 60 10 10 10 c 4*10 60 6*0 62 92 8c 16*0 10 28 44 82 82 82 fe 6*0 7c 82 5*80 82 82 7c
  //   10 8 70 0 0 0 44 44 0 5*82 86 7a 5*0 8 10 20 0 7c 82 82 fe 80 80 7e 5*0 10 28 44 0 7c 2 2 7e 82 82
  //   7e 6*0 44 44 0 7c 2 2 7e 82 82 7e 5*0 20 10 8 0 7c 2 2 7e 82 82 7e 5*0 18 24 18 0 7c 2 2 7e 82 82 7e
  //   9*0 7c 82 80 80 80 82 7c 10 8 70 0 0 10 28 44 0 7c 82 82 fe 80 80 7e 6*0 44 44 0 7c 82 82 fe 80 80
  //   7e 5*0 20 10 8 0 7c 82 82 fe 80 80 7e 6*0 48 48 0 70 5*10 7c 5*0 10 28 44 0 70 5*10 7c 5*0 40 20 10
  //   0 70 5*10 7c 4*0 44 44 0 38 44 82 82 82 fe 82 82 82 4*0 38 44 44 38 44 82 82 82 fe 82 82 82 4*0 c 30
  //   0 fe 80 80 80 fc 80 80 80 fe 9*0 6c 92 12 7e 90 90 6e 6*0 3e 48 88 88 fe 4*88 8e 5*0 10 28 44 0 7c
  //   5*82 7c 6*0 44 44 0 7c 5*82 7c 5*0 20 10 8 0 7c 5*82 7c 5*0 10 28 44 0 5*82 86 7a 5*0 20 10 8 0 5*82
  //   86 7a 6*0 44 44 0 5*82 86 7a 2 2 7c 0 44 44 0 7c 7*82 7c 4*0 44 44 0 8*82 7c 6*0 10 10 7c 82 80 80
  //   82 7c 10 10 6*0 38 44 40 40 f0 40 40 40 72 cc 6*0 82 82 44 28 10 7c 10 7c 10 10 6*0 f8 84 84 f8 80
  //   88 9c 88 88 84 6*0 c 12 10 10 10 7c 5*10 90 60 0 0 8 10 20 0 7c 2 2 7e 82 82 7e 5*0 8 10 20 0 70
  //   5*10 7c 5*0 8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
  //   Start hsync pulse at 28F
  //   End hsync pulse at 2EF
  //   End of scanline at 31F
  //   Start vsync pulse at 1EA
  //   End vsync pulse at 1EC
  //   End of frame at 0
  //   Readout address
endmodule

module HCount (
  input  CLK,
  input  nRST,
  output [11:0] HCOUNT_OUT,
  output HCOUNT_END,
  output BeginPulse,
  output EndPulse,
  output HVisEnd,
  output BeginActive,
  output EndActive
);

  wire n74163_1_pin1, n74163_1_pin3, n74163_1_pin7, n74163_1_pin15, n74163_2_pin15;

  _74163 #(.ShowInternalStructure("true")) u_74163_1 (
    .pin1(n74163_1_pin1), .pin2(CLK), .pin3(n74163_1_pin3), .pin4(n74163_1_pin3), .pin5(n74163_1_pin3),
    .pin6(n74163_1_pin3), .pin7(n74163_1_pin7), .pin15(n74163_1_pin15), .pin14(HCOUNT_OUT[0]),
    .pin13(HCOUNT_OUT[1]), .pin12(HCOUNT_OUT[2]), .pin11(HCOUNT_OUT[3]), .pin10(n74163_1_pin7),
    .pin9(n74163_1_pin7));
  _74163 #(.ShowInternalStructure("true")) u_74163_2 (
    .pin1(n74163_1_pin1), .pin2(CLK), .pin3(n74163_1_pin3), .pin4(n74163_1_pin3), .pin5(n74163_1_pin3),
    .pin6(n74163_1_pin3), .pin7(n74163_1_pin15), .pin15(n74163_2_pin15), .pin14(HCOUNT_OUT[4]),
    .pin13(HCOUNT_OUT[5]), .pin12(HCOUNT_OUT[6]), .pin11(HCOUNT_OUT[7]), .pin10(n74163_1_pin15),
    .pin9(n74163_1_pin7));
  _74163 #(.ShowInternalStructure("true")) u_74163_3 (
    .pin1(n74163_1_pin1), .pin2(CLK), .pin3(n74163_1_pin3), .pin4(n74163_1_pin3), .pin5(n74163_1_pin3),
    .pin6(n74163_1_pin3), .pin7(n74163_2_pin15), .pin14(HCOUNT_OUT[8]), .pin13(HCOUNT_OUT[9]),
    .pin12(HCOUNT_OUT[10]), .pin11(HCOUNT_OUT[11]), .pin10(n74163_2_pin15), .pin9(n74163_1_pin7));  // open: pin15
  HCntCtrl hcntctrl_1 (
    .HCOUNT(HCOUNT_OUT), .nRST(nRST), .HCOUNT_END(HCOUNT_END), .nHCCLR(n74163_1_pin1),
    .BeginPulse(BeginPulse), .EndPulse(EndPulse), .HVisEnd(HVisEnd), .BeginActive(BeginActive),
    .EndActive(EndActive));
  // also tied to GND on the sheet: n74163_1_pin3
  // also tied to VCC on the sheet: n74163_1_pin7

  // Notes on the sheet:
  //   Counters reset when nRST or HCOUNT_END asserted
endmodule

module VCount (
  input  CLK,
  input  nRST,
  input  HCOUNT_END,
  input  VCOUNT_INCR,
  output [11:0] VCOUNT_OUT,
  output VCOUNT_END,
  output BeginPulse,
  output EndPulse,
  output VVisEnd,
  output VCOUNT_ZERO,
  output VEndActive
);

  wire n74163_1_pin1, n74163_1_pin7, n74163_1_pin15, n74163_2_pin15, n74163_3_pin5;
  wire [9:0] n74163_1_pin3;

  _74163 #(.ShowInternalStructure("true")) u_74163_1 (
    .pin1(n74163_1_pin1), .pin2(CLK), .pin3(n74163_1_pin3[0]), .pin4(n74163_1_pin3[1]),
    .pin5(n74163_1_pin3[2]), .pin6(n74163_1_pin3[3]), .pin7(n74163_1_pin7), .pin15(n74163_1_pin15),
    .pin14(VCOUNT_OUT[0]), .pin13(VCOUNT_OUT[1]), .pin12(VCOUNT_OUT[2]), .pin11(VCOUNT_OUT[3]),
    .pin10(VCOUNT_INCR), .pin9(nRST));
  _74163 #(.ShowInternalStructure("true")) u_74163_2 (
    .pin1(n74163_1_pin1), .pin2(CLK), .pin3(n74163_1_pin3[4]), .pin4(n74163_1_pin3[5]),
    .pin5(n74163_1_pin3[6]), .pin6(n74163_1_pin3[7]), .pin7(n74163_1_pin15), .pin15(n74163_2_pin15),
    .pin14(VCOUNT_OUT[4]), .pin13(VCOUNT_OUT[5]), .pin12(VCOUNT_OUT[6]), .pin11(VCOUNT_OUT[7]),
    .pin10(n74163_1_pin15), .pin9(nRST));
  VCntCtrl vcntctrl_1 (
    .VCOUNT(VCOUNT_OUT), .HCOUNT_END(HCOUNT_END), .VCOUNT_INCR(VCOUNT_INCR), .VCOUNT_END(VCOUNT_END),
    .nVCCLR(n74163_1_pin1), .BeginPulse(BeginPulse), .EndPulse(EndPulse), .VVisEnd(VVisEnd),
    .VCOUNT_ZERO(VCOUNT_ZERO), .VEndActive(VEndActive));
  _74163 #(.ShowInternalStructure("true")) u_74163_3 (
    .pin1(n74163_1_pin1), .pin2(CLK), .pin3(n74163_1_pin3[8]), .pin4(n74163_1_pin3[9]), .pin5(n74163_3_pin5),
    .pin6(n74163_3_pin5), .pin7(n74163_2_pin15), .pin14(VCOUNT_OUT[8]), .pin13(VCOUNT_OUT[9]),
    .pin12(VCOUNT_OUT[10]), .pin11(VCOUNT_OUT[11]), .pin10(n74163_2_pin15), .pin9(nRST));  // open: pin15
  // also tied to GND on the sheet: {n74163_1_pin3[2], n74163_1_pin3[4], n74163_1_pin3[5], n74163_1_pin3[6], n74163_1_pin3[7], n74163_1_pin3[8], n74163_3_pin5}
  // also tied to VCC on the sheet: {n74163_1_pin3[0], n74163_1_pin3[1], n74163_1_pin3[3], n74163_1_pin3[9], n74163_1_pin7}

  // Notes on the sheet:
  //   Initial VCOUNT
endmodule

module HCntCtrl (
  input  [11:0] HCOUNT,
  input  nRST,
  output HCOUNT_END,
  output nHCCLR,
  output BeginPulse,
  output EndPulse,
  output HVisEnd,
  output BeginActive,
  output EndActive
);

  wire not_1_out, not_2_out, not_3_out, not_4_out, not_5_out, not_6_out, not_7_out, not_8_out, not_9_out,
       not_10_out, not_11_out, not_12_out, or_1_out;

  not not_1 (not_1_out, HCOUNT[5]);
  not not_2 (not_2_out, HCOUNT[4]);
  not not_3 (not_3_out, HCOUNT[8]);
  not not_4 (not_4_out, HCOUNT[4]);
  not not_5 (not_5_out, HCOUNT[8]);
  not not_6 (not_6_out, HCOUNT[6]);
  not not_7 (not_7_out, HCOUNT[5]);
  not not_8 (not_8_out, HCOUNT[8]);
  not not_9 (not_9_out, HCOUNT[7]);
  not not_10 (not_10_out, nRST);
  not not_11 (not_11_out, HCOUNT[6]);
  not not_12 (not_12_out, HCOUNT[7]);
  Comparator #(.mode("unsigned"), .width(12)) comparator_1 (.a(HCOUNT), .b(12'h319), .eq(BeginActive));  // open: gt, lt
  Comparator #(.mode("unsigned"), .width(12)) comparator_2 (.a(HCOUNT), .b(12'h279), .eq(EndActive));  // open: gt, lt
  and and_1 (HCOUNT_END, HCOUNT[0], HCOUNT[1], HCOUNT[2], HCOUNT[3], HCOUNT[4], not_1_out, not_6_out, not_9_out, HCOUNT[8], HCOUNT[9]);
  or or_1 (or_1_out, not_10_out, HCOUNT_END);
  and and_2 (BeginPulse, HCOUNT[0], HCOUNT[1], HCOUNT[2], HCOUNT[3], not_2_out, not_7_out, not_11_out, HCOUNT[7], not_3_out, HCOUNT[9]);
  and and_3 (EndPulse, HCOUNT[0], HCOUNT[1], HCOUNT[2], HCOUNT[3], not_4_out, HCOUNT[5], HCOUNT[6], HCOUNT[7], not_5_out, HCOUNT[9]);
  and and_4 (HVisEnd, HCOUNT[0], HCOUNT[1], HCOUNT[2], HCOUNT[3], HCOUNT[4], HCOUNT[5], HCOUNT[6], not_12_out, not_8_out, HCOUNT[9]);
  not not_13 (nHCCLR, or_1_out);

  // Notes on the sheet:
  //   This circuit is intended to be equivalent to HCntCtrl.pld
  //   Counters cleared when nRST asserted or HCOUNT_END asserted
  //   HVisEnd asserted when HCOUNT=639
  //   HCOUNT_END asserted when HCOUNT=799
  //   BeginPulse asserted when HCOUNT=655
  //   EndPulse asserted when HCOUNT=751
  //   BeginActive when HCOUNT=793
  //   EndActive when HCOUNT=633
endmodule

module VCntCtrl (
  input  [11:0] VCOUNT,
  input  HCOUNT_END,
  input  VCOUNT_INCR,
  output VCOUNT_END,
  output nVCCLR,
  output BeginPulse,
  output EndPulse,
  output VVisEnd,
  output VCOUNT_ZERO,
  output VEndActive
);

  wire and_1_out, not_1_out, not_2_out, not_3_out, not_4_out, not_5_out, not_6_out, not_7_out, not_8_out,
       not_9_out, not_10_out, not_11_out, not_12_out, not_13_out, not_14_out, not_15_out, not_16_out,
       not_17_out, not_18_out, not_19_out, not_20_out, not_21_out, not_22_out, not_23_out, not_24_out,
       not_25_out, not_26_out, not_27_out;

  not not_1 (not_1_out, VCOUNT[0]);
  not not_2 (not_2_out, VCOUNT[1]);
  not not_3 (not_3_out, VCOUNT[4]);
  not not_4 (not_4_out, VCOUNT[5]);
  not not_5 (not_5_out, VCOUNT[0]);
  not not_6 (not_6_out, VCOUNT[2]);
  not not_7 (not_7_out, VCOUNT[0]);
  not not_8 (not_8_out, VCOUNT[1]);
  not not_9 (not_9_out, VCOUNT[0]);
  not not_10 (not_10_out, VCOUNT[1]);
  not not_11 (not_11_out, VCOUNT[0]);
  not not_12 (not_12_out, VCOUNT[1]);
  not not_13 (not_13_out, VCOUNT[7]);
  not not_14 (not_14_out, VCOUNT[8]);
  not not_15 (not_15_out, VCOUNT[6]);
  not not_16 (not_16_out, VCOUNT[7]);
  not not_17 (not_17_out, VCOUNT[4]);
  not not_18 (not_18_out, VCOUNT[4]);
  not not_19 (not_19_out, VCOUNT[2]);
  not not_20 (not_20_out, VCOUNT[3]);
  not not_21 (not_21_out, VCOUNT[2]);
  not not_22 (not_22_out, VCOUNT[3]);
  not not_23 (not_23_out, VCOUNT[8]);
  and and_1 (and_1_out, VCOUNT_END, VCOUNT_INCR);
  not not_24 (not_24_out, VCOUNT[4]);
  not not_25 (not_25_out, VCOUNT[4]);
  not not_26 (not_26_out, VCOUNT[5]);
  not not_27 (not_27_out, VCOUNT[6]);
  and and_2 (VCOUNT_END, not_1_out, not_2_out, VCOUNT[2], VCOUNT[3], not_3_out, not_4_out, not_15_out, not_16_out, not_23_out, VCOUNT[9]);
  not not_28 (nVCCLR, and_1_out);
  and and_3 (BeginPulse, HCOUNT_END, not_5_out, VCOUNT[1], not_6_out, VCOUNT[3], not_17_out, VCOUNT[5], VCOUNT[6], VCOUNT[7], VCOUNT[8]);
  and and_4 (EndPulse, HCOUNT_END, not_7_out, not_8_out, VCOUNT[2], VCOUNT[3], not_18_out, VCOUNT[5], VCOUNT[6], VCOUNT[7], VCOUNT[8]);
  and and_5 (VVisEnd, not_9_out, not_10_out, not_19_out, not_20_out, not_24_out, VCOUNT[5], VCOUNT[6], VCOUNT[7], VCOUNT[8]);
  and and_6 (VCOUNT_ZERO, not_11_out, not_12_out, not_21_out, not_22_out, not_25_out, not_26_out, not_27_out, not_13_out, not_14_out);
  Comparator #(.mode("unsigned"), .width(12)) comparator_1 (.a(VCOUNT), .b(12'h1df), .eq(VEndActive));  // open: gt, lt

  // Notes on the sheet:
  //   This circuit is intended to be equivalent to VCntCtrl.pld
  //   Clear counters if (VCOUNT_INCR & VCOUNT_END)
  //   VVisEnd generated when VCOUNT=480 (binary 111100000)
  //   VCOUNT_ZERO generated when VCOUNT=0
  //   BeginPulse when HCOUNT_END and VCOUNT=490 (binary 111101010)
  //   EndPulse when HCOUNT_END and VCOUNT=492 (binary 111101100)
  //   VCOUNT_END when count is 524
endmodule

module Sync (
  input  CLK,
  input  nRST,
  input  HBeginPulse,
  input  HEndPulse,
  input  VBeginPulse,
  input  VEndPulse,
  input  HCOUNT_END,
  input  VCOUNT_ZERO,
  input  HVisEnd,
  input  VVisEnd,
  input  VCOUNT_END,
  input  VEndActive,
  output HSYNC_OUT,
  output VSYNC_OUT,
  output HVis,
  output VVis,
  output Vis,
  output VActive
);

  wire and_1_out, and_2_out, and_3_out, and_4_out, and_5_out, and_6_out, and_7_out, and_8_out, and_9_out,
       not_1_out, not_2_out, not_3_out, not_4_out, not_5_out, not_6_out, not_7_out, not_8_out, not_9_out,
       not_10_out, not_11_out, not_12_out, or_1_out, or_2_out, or_3_out, or_4_out, or_5_out;

  not not_1 (not_1_out, VEndActive);
  not not_2 (not_2_out, HBeginPulse);
  not not_3 (not_3_out, HEndPulse);
  not not_4 (not_4_out, VBeginPulse);
  not not_5 (not_5_out, VEndPulse);
  not not_6 (not_6_out, nRST);
  not not_7 (not_7_out, VVisEnd);
  not not_8 (not_8_out, HCOUNT_END);
  not not_9 (not_9_out, HCOUNT_END);
  not not_10 (not_10_out, HVisEnd);
  and and_1 (and_1_out, nRST, HCOUNT_END, VCOUNT_ZERO);
  and and_2 (and_2_out, nRST, not_7_out, VVis);
  and and_3 (and_3_out, nRST, VVisEnd, not_8_out, VVis);
  and and_4 (and_4_out, nRST, HCOUNT_END, VCOUNT_END);
  and and_5 (and_5_out, nRST, not_1_out, VActive);
  and and_6 (and_6_out, nRST, VEndActive, not_9_out, VActive);
  and and_7 (and_7_out, not_2_out, not_3_out, HSYNC_OUT);
  and and_8 (and_8_out, not_4_out, not_5_out, VSYNC_OUT);
  and and_9 (and_9_out, not_10_out, HVis);
  or or_1 (or_1_out, not_11_out, HEndPulse, and_7_out);
  or or_2 (or_2_out, not_12_out, VEndPulse, and_8_out);
  D_Flip_Flop d_ff_1 (.D(or_3_out), .clk(CLK), .Q(HVis), .preset(1'b0), .reset(1'b0));  // open: Qn
  or or_3 (or_3_out, not_6_out, HCOUNT_END, and_9_out);
  D_Flip_Flop d_ff_2 (.D(or_4_out), .clk(CLK), .Q(VVis), .preset(1'b0), .reset(1'b0));  // open: Qn
  or or_4 (or_4_out, and_1_out, and_2_out, and_3_out);
  or or_5 (or_5_out, and_4_out, and_5_out, and_6_out);
  not not_11 (not_11_out, nRST);
  D_Flip_Flop d_ff_3 (.D(or_1_out), .clk(CLK), .Q(HSYNC_OUT), .preset(1'b0), .reset(1'b0));  // open: Qn
  not not_12 (not_12_out, nRST);
  D_Flip_Flop d_ff_4 (.D(or_2_out), .clk(CLK), .Q(VSYNC_OUT), .preset(1'b0), .reset(1'b0));  // open: Qn
  D_Flip_Flop d_ff_5 (.D(or_5_out), .clk(CLK), .Q(VActive), .preset(1'b0), .reset(1'b0));  // open: Qn
  and and_10 (Vis, HVis, VVis);

  // Notes on the sheet:
  //   This circuit is intended to be equivalent to Sync.pld
  //   VVis is initially false
  //    (VCOUNT starts in back porch)
endmodule

module ReadoutCtrl (
  input  CLK,
  input  nRST,
  input  VActive,
  input  HBeginActive,
  input  HEndActive,
  input  [3:0] VCOUNT,
  input  RowBeginA12,
  input  VSync,
  input  HBeginPulse,
  input  ReadoutTCnt,
  output Active,
  output Count0,
  output Count1,
  output Phase,
  output UpdateRowBeginCP,
  output nLoadReadoutAddr,
  output IncrReadoutAddr,
  output ReadoutA12,
  output nClearRowBeginAddr
);

  wire and_1_out, and_2_out, and_3_out, and_4_out, and_5_out, and_6_out, and_7_out, and_8_out, and_9_out,
       and_10_out, and_11_out, and_12_out, and_13_out, and_14_out, and_15_out, and_16_out, and_17_out,
       and_18_out, and_20_out, and_21_out, d_ff_6_q, not_1_out, not_2_out, not_3_out, not_4_out, not_5_out,
       not_6_out, not_7_out, not_8_out, not_9_out, not_10_out, not_11_out, not_12_out, not_14_out,
       not_15_out, or_1_out, or_2_out, or_3_out, or_4_out, or_5_out;

  not not_1 (not_1_out, Active);
  not not_2 (not_2_out, VCOUNT[0]);
  not not_3 (not_3_out, VCOUNT[1]);
  not not_4 (not_4_out, VCOUNT[2]);
  not not_5 (not_5_out, VCOUNT[3]);
  not not_6 (not_6_out, Count0);
  not not_7 (not_7_out, Count1);
  not not_8 (not_8_out, ReadoutTCnt);
  not not_9 (not_9_out, HEndActive);
  not not_10 (not_10_out, Active);
  not not_11 (not_11_out, nLoadReadoutAddr);
  and and_1 (and_1_out, VSync, nRST);
  and and_2 (and_2_out, Active, Count0, not_15_out);
  and and_3 (and_3_out, Active, not_14_out, Count1);
  and and_4 (and_4_out, Active, Count0, Count1, not_12_out);
  and and_5 (and_5_out, Active, not_15_out, Phase);
  and and_6 (and_6_out, Active, not_14_out, Phase);
  and and_7 (and_7_out, VActive, HBeginPulse, not_2_out);
  and and_8 (and_8_out, VActive, HBeginPulse, not_3_out);
  and and_9 (and_9_out, VActive, HBeginPulse, not_4_out);
  and and_10 (and_10_out, VActive, HBeginPulse, not_5_out);
  and and_11 (and_11_out, Active, not_6_out, not_7_out, ReadoutTCnt);
  and and_12 (and_12_out, not_11_out, RowBeginA12);
  and and_13 (and_13_out, nLoadReadoutAddr, not_10_out, ReadoutA12);
  and and_14 (and_14_out, nLoadReadoutAddr, Count0, ReadoutA12);
  and and_15 (and_15_out, nLoadReadoutAddr, Count1, ReadoutA12);
  and and_16 (and_16_out, nLoadReadoutAddr, not_8_out, ReadoutA12);
  and and_17 (and_17_out, nRST, not_9_out, Active, VActive);
  and and_18 (and_18_out, nRST, HBeginActive, VActive);
  and and_19 (IncrReadoutAddr, Active, not_6_out, not_7_out);
  and and_20 (and_20_out, Active, not_14_out);
  or or_1 (or_1_out, not_1_out, and_2_out, and_3_out);
  or or_2 (or_2_out, and_4_out, and_5_out, and_6_out);
  and and_21 (and_21_out, VActive, HBeginPulse, VCOUNT[0], VCOUNT[1], VCOUNT[2], VCOUNT[3]);
  or or_3 (or_3_out, and_7_out, and_8_out, and_9_out, and_10_out);
  or or_4 (or_4_out, and_11_out, and_12_out, and_13_out, and_14_out, and_15_out, and_16_out);
  D_Flip_Flop d_ff_1 (.D(or_5_out), .clk(CLK), .Q(Active), .preset(1'b0), .reset(1'b0));  // open: Qn
  or or_5 (or_5_out, and_17_out, and_18_out);
  D_Flip_Flop d_ff_2 (.D(and_20_out), .clk(CLK), .Q(Count0), .preset(1'b0), .reset(1'b0));  // open: Qn
  D_Flip_Flop d_ff_3 (.D(or_1_out), .clk(CLK), .Q(Count1), .preset(1'b0), .reset(1'b0));  // open: Qn
  D_Flip_Flop d_ff_4 (.D(or_2_out), .clk(CLK), .Q(Phase), .preset(1'b0), .reset(1'b0));  // open: Qn
  D_Flip_Flop d_ff_5 (.D(and_21_out), .clk(CLK), .Q(UpdateRowBeginCP), .preset(1'b0), .reset(1'b0));  // open: Qn
  D_Flip_Flop d_ff_6 (.D(or_3_out), .clk(CLK), .Q(d_ff_6_q), .preset(1'b0), .reset(1'b0));  // open: Qn
  D_Flip_Flop d_ff_7 (.D(or_4_out), .clk(CLK), .Q(ReadoutA12), .preset(1'b0), .reset(1'b0));  // open: Qn
  D_Flip_Flop d_ff_8 (.D(and_1_out), .clk(CLK), .Q(nClearRowBeginAddr), .preset(1'b0), .reset(1'b0));  // open: Qn
  not not_12 (not_12_out, Phase);
  not not_13 (nLoadReadoutAddr, d_ff_6_q);
  LED led_1 (.in(Count0));
  not not_14 (not_14_out, Count0);
  LED led_2 (.in(Count1));
  not not_15 (not_15_out, Count1);
  LED led_3 (.in(Phase));
endmodule

module Readout (
  input  VSync,
  input  CLK,
  input  nRST,
  input  VActive,
  input  HBeginActive,
  input  HEndActive,
  input  [3:0] VCOUNT,
  input  HBeginPulse,
  output Active,
  output Count0,
  output Count1,
  output Phase,
  output [12:0] ReadoutAddr,
  output [12:0] RowBeginAddr,
  output UpdateRowBeginCP
);

  wire IncrReadoutAddr, n74163_1_pin1, n74163_1_pin15, n74163_2_pin15, n74273_2_pin18, nClearRowBeginAddr,
       nLoadReadoutAddr, ReadoutTCnt;

  _74163 #(.ShowInternalStructure("true")) u_74163_1 (
    .pin1(n74163_1_pin1), .pin2(CLK), .pin3(RowBeginAddr[0]), .pin4(RowBeginAddr[1]), .pin5(RowBeginAddr[2]),
    .pin6(RowBeginAddr[3]), .pin7(IncrReadoutAddr), .pin15(n74163_1_pin15), .pin14(ReadoutAddr[0]),
    .pin13(ReadoutAddr[1]), .pin12(ReadoutAddr[2]), .pin11(ReadoutAddr[3]), .pin10(IncrReadoutAddr),
    .pin9(nLoadReadoutAddr));
  _74163 #(.ShowInternalStructure("true")) u_74163_2 (
    .pin1(n74163_1_pin1), .pin2(CLK), .pin3(RowBeginAddr[4]), .pin4(RowBeginAddr[5]), .pin5(RowBeginAddr[6]),
    .pin6(RowBeginAddr[7]), .pin7(n74163_1_pin15), .pin15(n74163_2_pin15), .pin14(ReadoutAddr[4]),
    .pin13(ReadoutAddr[5]), .pin12(ReadoutAddr[6]), .pin11(ReadoutAddr[7]), .pin10(n74163_1_pin15),
    .pin9(nLoadReadoutAddr));
  _74273 #(.ShowInternalStructure("true")) u_74273_1 (
    .pin1(nClearRowBeginAddr), .pin2(RowBeginAddr[0]), .pin3(ReadoutAddr[0]), .pin4(ReadoutAddr[1]),
    .pin5(RowBeginAddr[1]), .pin6(RowBeginAddr[2]), .pin7(ReadoutAddr[2]), .pin8(ReadoutAddr[3]),
    .pin9(RowBeginAddr[3]), .pin19(RowBeginAddr[7]), .pin18(ReadoutAddr[7]), .pin17(ReadoutAddr[6]),
    .pin16(RowBeginAddr[6]), .pin15(RowBeginAddr[5]), .pin14(ReadoutAddr[5]), .pin13(ReadoutAddr[4]),
    .pin12(RowBeginAddr[4]), .pin11(UpdateRowBeginCP));
  ReadoutCtrl readoutctrl_1 (
    .CLK(CLK), .nRST(nRST), .VActive(VActive), .HBeginActive(HBeginActive), .HEndActive(HEndActive),
    .VCOUNT(VCOUNT), .RowBeginA12(RowBeginAddr[12]), .VSync(VSync), .HBeginPulse(HBeginPulse),
    .ReadoutTCnt(ReadoutTCnt), .Active(Active), .Count0(Count0), .Count1(Count1), .Phase(Phase),
    .UpdateRowBeginCP(UpdateRowBeginCP), .nLoadReadoutAddr(nLoadReadoutAddr),
    .IncrReadoutAddr(IncrReadoutAddr), .ReadoutA12(ReadoutAddr[12]), .nClearRowBeginAddr(nClearRowBeginAddr));
  _74163 #(.ShowInternalStructure("true")) u_74163_3 (
    .pin1(n74163_1_pin1), .pin2(CLK), .pin3(RowBeginAddr[8]), .pin4(RowBeginAddr[9]),
    .pin5(RowBeginAddr[10]), .pin6(RowBeginAddr[11]), .pin7(n74163_2_pin15), .pin15(ReadoutTCnt),
    .pin14(ReadoutAddr[8]), .pin13(ReadoutAddr[9]), .pin12(ReadoutAddr[10]), .pin11(ReadoutAddr[11]),
    .pin10(n74163_2_pin15), .pin9(nLoadReadoutAddr));
  _74273 #(.ShowInternalStructure("true")) u_74273_2 (
    .pin1(nClearRowBeginAddr), .pin2(RowBeginAddr[8]), .pin3(ReadoutAddr[8]), .pin4(ReadoutAddr[9]),
    .pin5(RowBeginAddr[9]), .pin6(RowBeginAddr[10]), .pin7(ReadoutAddr[10]), .pin8(ReadoutAddr[11]),
    .pin9(RowBeginAddr[11]), .pin18(n74273_2_pin18), .pin17(n74273_2_pin18), .pin14(n74273_2_pin18),
    .pin13(ReadoutAddr[12]), .pin12(RowBeginAddr[12]), .pin11(UpdateRowBeginCP));  // open: pin19, pin16, pin15
  // also tied to GND on the sheet: n74273_2_pin18
  // also tied to VCC on the sheet: n74163_1_pin1

  // Other names for the same wires on the sheet: ReadoutA12 = ReadoutAddr[12]; RowBeginA12 = RowBeginAddr[12]
endmodule
