// Logisim project hw_vga_sim.circ as structural Verilog: 8 circuits, main circuit main
module main (
  input  nRST
);

  wire CLK_out, HBeginPulse, HCOUNT_END, HEndPulse, sync_1_hsync_out, sync_1_vsync_out, VBeginPulse,
       VEndPulse;
  wire [11:0] HCOUNT_OUT, VCOUNT_OUT;

  Clock CLK (.out(CLK_out));
  HCount hcount_1 (
    .CLK(CLK_out), .nRST(nRST), .HCOUNT_OUT(HCOUNT_OUT), .HCOUNT_END(HCOUNT_END), .BeginPulse(HBeginPulse),
    .EndPulse(HEndPulse));  // open: nHCOUNT_END
  VCount vcount_1 (
    .CLK(CLK_out), .nRST(nRST), .HCOUNT_END(HCOUNT_END), .VCOUNT_OUT(VCOUNT_OUT), .BeginPulse(VBeginPulse),
    .EndPulse(VEndPulse));  // open: VCOUNT_END, nVCOUNT_END
  Sync sync_1 (
    .CLK(CLK_out), .nRST(nRST), .HCOUNT_END(HCOUNT_END), .HBeginPulse(HBeginPulse), .HEndPulse(HEndPulse),
    .VBeginPulse(VBeginPulse), .VEndPulse(VEndPulse), .HSYNC_OUT(sync_1_hsync_out),
    .VSYNC_OUT(sync_1_vsync_out));
  LED led_1 (.in(sync_1_hsync_out));
  LED led_2 (.in(sync_1_vsync_out));
  Hex_Digit_Display hex_digit_display_1 (.value(HCOUNT_OUT[11:8]));  // open: dp
  Hex_Digit_Display hex_digit_display_2 (.value(VCOUNT_OUT[11:8]));  // open: dp
  Hex_Digit_Display hex_digit_display_3 (.value(HCOUNT_OUT[7:4]));  // open: dp
  Hex_Digit_Display hex_digit_display_4 (.value(HCOUNT_OUT[3:0]));  // open: dp
  Hex_Digit_Display hex_digit_display_5 (.value(VCOUNT_OUT[7:4]));  // open: dp
  Hex_Digit_Display hex_digit_display_6 (.value(VCOUNT_OUT[3:0]));  // open: dp
endmodule

module HCount (
  input  CLK,
  input  nRST,
  output [11:0] HCOUNT_OUT,
  output HCOUNT_END,
  output nHCOUNT_END,
  output BeginPulse,
  output EndPulse
);

  wire n74163_1_pin1, n74163_1_pin3, n74163_1_pin7, n74163_1_pin15, n74163_2_pin15;

  _74163 #(.ShowInternalStructure("true")) u_74163_1 (
    .pin1(n74163_1_pin1), .pin2(CLK), .pin3(n74163_1_pin3), .pin4(n74163_1_pin3), .pin5(n74163_1_pin3),
    .pin6(n74163_1_pin3), .pin7(n74163_1_pin7), .pin15(n74163_1_pin15), .pin14(HCOUNT_OUT[0]),
    .pin13(HCOUNT_OUT[1]), .pin12(HCOUNT_OUT[2]), .pin11(HCOUNT_OUT[3]), .pin10(n74163_1_pin7),
    .pin9(n74163_1_pin7));
  _74163 #(.ShowInternalStructure("true")) u_74163_2 (
    .pin1(n74163_1_pin1), .pin2(CLK), .pin3(n74163_1_pin3), .pin4(n74163_1_pin3), .pin5(n74163_1_pin3),
    .pin6(n74163_1_pin3), .pin7(n74163_1_pin15), .pin15(n74163_2_pin15), .pin14(HCOUNT_OUT[4]),
    .pin13(HCOUNT_OUT[5]), .pin12(HCOUNT_OUT[6]), .pin11(HCOUNT_OUT[7]), .pin10(n74163_1_pin15),
    .pin9(n74163_1_pin7));
  _74163 #(.ShowInternalStructure("true")) u_74163_3 (
    .pin1(n74163_1_pin1), .pin2(CLK), .pin3(n74163_1_pin3), .pin4(n74163_1_pin3), .pin5(n74163_1_pin3),
    .pin6(n74163_1_pin3), .pin7(n74163_2_pin15), .pin14(HCOUNT_OUT[8]), .pin13(HCOUNT_OUT[9]),
    .pin12(HCOUNT_OUT[10]), .pin11(HCOUNT_OUT[11]), .pin10(n74163_2_pin15), .pin9(n74163_1_pin7));  // open: pin15
  HCntCtrl hcntctrl_1 (
    .HCOUNT(HCOUNT_OUT), .nRST(nRST), .HCOUNT_END(HCOUNT_END), .nHCOUNT_END(nHCOUNT_END),
    .nHCCLR(n74163_1_pin1), .BeginPulse(BeginPulse), .EndPulse(EndPulse));
  // also tied to GND on the sheet: n74163_1_pin3
  // also tied to VCC on the sheet: n74163_1_pin7

  // Notes on the sheet:
  //   Counters reset when nRST or nHCOUNT_END asserted
endmodule

module VCount (
  input  CLK,
  input  nRST,
  input  HCOUNT_END,
  output [11:0] VCOUNT_OUT,
  output VCOUNT_END,
  output nVCOUNT_END,
  output BeginPulse,
  output EndPulse
);

  wire n74163_1_pin1, n74163_1_pin3, n74163_1_pin7, n74163_1_pin9, n74163_1_pin15, n74163_2_pin15;

  _74163 #(.ShowInternalStructure("true")) u_74163_1 (
    .pin1(n74163_1_pin1), .pin2(CLK), .pin3(n74163_1_pin3), .pin4(n74163_1_pin3), .pin5(n74163_1_pin3),
    .pin6(n74163_1_pin3), .pin7(n74163_1_pin7), .pin15(n74163_1_pin15), .pin14(VCOUNT_OUT[0]),
    .pin13(VCOUNT_OUT[1]), .pin12(VCOUNT_OUT[2]), .pin11(VCOUNT_OUT[3]), .pin10(HCOUNT_END),
    .pin9(n74163_1_pin9));
  _74163 #(.ShowInternalStructure("true")) u_74163_2 (
    .pin1(n74163_1_pin1), .pin2(CLK), .pin3(n74163_1_pin3), .pin4(n74163_1_pin3), .pin5(n74163_1_pin3),
    .pin6(n74163_1_pin3), .pin7(n74163_1_pin15), .pin15(n74163_2_pin15), .pin14(VCOUNT_OUT[4]),
    .pin13(VCOUNT_OUT[5]), .pin12(VCOUNT_OUT[6]), .pin11(VCOUNT_OUT[7]), .pin10(n74163_1_pin15),
    .pin9(n74163_1_pin9));
  VCntCtrl vcntctrl_1 (
    .nRST(nRST), .VCOUNT(VCOUNT_OUT), .HCOUNT_END(HCOUNT_END), .VCOUNT_END(VCOUNT_END),
    .nVCOUNT_END(nVCOUNT_END), .nVCCLR(n74163_1_pin1), .BeginPulse(BeginPulse), .EndPulse(EndPulse));
  _74163 #(.ShowInternalStructure("true")) u_74163_3 (
    .pin1(n74163_1_pin1), .pin2(CLK), .pin3(n74163_1_pin3), .pin4(n74163_1_pin3), .pin5(n74163_1_pin3),
    .pin6(n74163_1_pin3), .pin7(n74163_2_pin15), .pin14(VCOUNT_OUT[8]), .pin13(VCOUNT_OUT[9]),
    .pin12(VCOUNT_OUT[10]), .pin11(VCOUNT_OUT[11]), .pin10(n74163_2_pin15), .pin9(n74163_1_pin9));  // open: pin15
  // also tied to GND on the sheet: n74163_1_pin3
  // also tied to VCC on the sheet: {n74163_1_pin7, n74163_1_pin9}

  // Notes on the sheet:
  //   Counters reset if nRST asserted or (VCOUNT_END & HCOUNT_END)
endmodule

module HSync (
  input  CLK,
  input  nRST,
  input  BeginPulse,
  input  EndPulse,
  output HSYNC_OUT
);

  wire and_1_out, not_1_out, not_2_out, not_3_out, or_1_out;

  not not_1 (not_1_out, BeginPulse);
  not not_2 (not_2_out, EndPulse);
  and and_1 (and_1_out, not_1_out, not_2_out, HSYNC_OUT);
  or or_1 (or_1_out, not_3_out, EndPulse, and_1_out);
  not not_3 (not_3_out, nRST);
  D_Flip_Flop d_ff_1 (.D(or_1_out), .clk(CLK), .Q(HSYNC_OUT), .preset(not_3_out), .reset(1'b0));  // open: Qn

  // Notes on the sheet:
  //   This circuit is intended to replicate the logic in HSync.pld
endmodule

module VSync (
  input  CLK,
  input  BeginPulse,
  input  EndPulse,
  input  nRST,
  output VSYNC_OUT
);

  wire and_1_out, not_1_out, not_2_out, not_3_out, or_1_out;

  not not_1 (not_1_out, BeginPulse);
  not not_2 (not_2_out, EndPulse);
  or or_1 (or_1_out, not_3_out, EndPulse, and_1_out);
  and and_1 (and_1_out, not_1_out, not_2_out, VSYNC_OUT);
  D_Flip_Flop d_ff_1 (.D(or_1_out), .clk(CLK), .Q(VSYNC_OUT), .preset(not_3_out), .reset(1'b0));  // open: Qn
  not not_3 (not_3_out, nRST);

  // Notes on the sheet:
  //   This circuit is intended to replicate the logic in VSync.pld
endmodule

module HCntCtrl (
  input  [11:0] HCOUNT,
  input  nRST,
  output HCOUNT_END,
  output nHCOUNT_END,
  output nHCCLR,
  output BeginPulse,
  output EndPulse
);

  wire not_1_out, not_2_out, not_3_out, not_4_out, not_5_out, not_6_out, not_7_out, not_8_out, not_9_out,
       not_10_out, or_1_out;

  not not_1 (not_1_out, HCOUNT[5]);
  not not_2 (not_2_out, HCOUNT[4]);
  not not_3 (not_3_out, HCOUNT[8]);
  not not_4 (not_4_out, HCOUNT[4]);
  not not_5 (not_5_out, HCOUNT[8]);
  not not_6 (not_6_out, HCOUNT[6]);
  not not_7 (not_7_out, HCOUNT[5]);
  not not_8 (not_8_out, HCOUNT[7]);
  not not_9 (not_9_out, nRST);
  not not_10 (not_10_out, HCOUNT[6]);
  and and_1 (HCOUNT_END, HCOUNT[0], HCOUNT[1], HCOUNT[2], HCOUNT[3], HCOUNT[4], not_1_out, not_6_out, not_8_out, HCOUNT[8], HCOUNT[9]);
  or or_1 (or_1_out, not_9_out, HCOUNT_END);
  and and_2 (BeginPulse, HCOUNT[0], HCOUNT[1], HCOUNT[2], HCOUNT[3], not_2_out, not_7_out, not_10_out, HCOUNT[7], not_3_out, HCOUNT[9]);
  and and_3 (EndPulse, HCOUNT[0], HCOUNT[1], HCOUNT[2], HCOUNT[3], not_4_out, HCOUNT[5], HCOUNT[6], HCOUNT[7], not_5_out, HCOUNT[9]);
  not not_11 (nHCOUNT_END, HCOUNT_END);
  not not_12 (nHCCLR, or_1_out);

  // Notes on the sheet:
  //   This circuit is intended to be equivalent to HCntCtrl.pld
  //   Counters cleared when nRST asserted or HCOUNT_END asserted
  //   HCOUNT_END asserted when HCOUNT=799
  //   BeginPulse asserted when HCOUNT=655
  //   EndPulse asserted when HCOUNT=751
endmodule

module VCntCtrl (
  input  nRST,
  input  [11:0] VCOUNT,
  input  HCOUNT_END,
  output VCOUNT_END,
  output nVCOUNT_END,
  output nVCCLR,
  output BeginPulse,
  output EndPulse
);

  wire and_1_out, and_3_out, and_4_out, comparator_1_eq, comparator_2_eq, not_1_out, not_2_out, not_3_out,
       not_4_out, not_5_out, not_6_out, not_7_out, not_8_out, not_9_out, not_10_out, not_11_out, not_12_out,
       not_13_out, or_1_out;

  not not_1 (not_1_out, nRST);
  not not_2 (not_2_out, VCOUNT[0]);
  not not_3 (not_3_out, VCOUNT[1]);
  not not_4 (not_4_out, VCOUNT[4]);
  not not_5 (not_5_out, VCOUNT[5]);
  and and_1 (and_1_out, VCOUNT_END, HCOUNT_END);
  not not_6 (not_6_out, VCOUNT[1]);
  not not_7 (not_7_out, VCOUNT[2]);
  not not_8 (not_8_out, VCOUNT[2]);
  not not_9 (not_9_out, VCOUNT[6]);
  not not_10 (not_10_out, VCOUNT[7]);
  not not_11 (not_11_out, VCOUNT[4]);
  not not_12 (not_12_out, VCOUNT[4]);
  not not_13 (not_13_out, VCOUNT[8]);
  or or_1 (or_1_out, not_1_out, and_1_out);
  and and_2 (VCOUNT_END, not_2_out, not_3_out, VCOUNT[2], VCOUNT[3], not_4_out, not_5_out, not_9_out, not_10_out, not_13_out, VCOUNT[9]);
  not not_14 (nVCCLR, or_1_out);
  and and_3 (and_3_out, HCOUNT_END, VCOUNT[0], not_6_out, not_7_out, VCOUNT[3], VCOUNT[5], VCOUNT[6], VCOUNT[7], VCOUNT[8]);
  and and_4 (and_4_out, HCOUNT_END, VCOUNT[0], VCOUNT[1], not_8_out, VCOUNT[3], VCOUNT[5], VCOUNT[6], VCOUNT[7], VCOUNT[8]);
  not not_15 (nVCOUNT_END, VCOUNT_END);
  Comparator #(.mode("unsigned"), .width(12)) comparator_1 (
    .a(VCOUNT), .b(12'h1e9), .eq(comparator_1_eq));  // open: gt, lt
  and and_5 (BeginPulse, comparator_1_eq, HCOUNT_END);
  Comparator #(.mode("unsigned"), .width(12)) comparator_2 (
    .a(VCOUNT), .b(12'h1eb), .eq(comparator_2_eq));  // open: gt, lt
  and and_6 (EndPulse, comparator_2_eq, HCOUNT_END);

  // Notes on the sheet:
  //   This circuit is intended to be equivalent to VCntCtrl.pld
  //   Clear counters if nRST asserted or (HCOUNT_END & VCOUNT_END)
  //   BeginPulse when HCOUNT_END and VCOUNT=489
  //   EndPulse when HCOUNT_END and VCOUNT=491
  //   VCOUNT_END when count is 524
endmodule

module Sync (
  input  CLK,
  input  nRST,
  input  HCOUNT_END,
  input  HBeginPulse,
  input  HEndPulse,
  input  VBeginPulse,
  input  VEndPulse,
  output HSYNC_OUT,
  output VSYNC_OUT
);

  wire and_1_out, and_2_out, not_1_out, not_2_out, not_3_out, not_4_out, not_5_out, not_6_out, or_1_out,
       or_2_out;

  not not_1 (not_1_out, HBeginPulse);
  not not_2 (not_2_out, HEndPulse);
  not not_3 (not_3_out, VBeginPulse);
  not not_4 (not_4_out, VEndPulse);
  and and_1 (and_1_out, not_1_out, not_2_out, HSYNC_OUT);
  and and_2 (and_2_out, not_3_out, not_4_out, VSYNC_OUT);
  or or_1 (or_1_out, not_5_out, HEndPulse, and_1_out);
  or or_2 (or_2_out, not_6_out, VEndPulse, and_2_out);
  not not_5 (not_5_out, nRST);
  D_Flip_Flop d_ff_1 (.D(or_1_out), .clk(CLK), .Q(HSYNC_OUT), .preset(not_5_out), .reset(1'b0));  // open: Qn
  not not_6 (not_6_out, nRST);
  D_Flip_Flop d_ff_2 (.D(or_2_out), .clk(CLK), .Q(VSYNC_OUT), .preset(not_6_out), .reset(1'b0));  // open: Qn
endmodule
